// Logisim project s5120196_Wenjin_Li_Logic_Circuit.circ as structural Verilog: 5 circuits, main circuit main
module main (
  input  S1,
  input  S2,
  input  S3,
  input  [2:0] number_of_games,
  input  [2:0] in_5,
  input  S4,
  output out_7,
  output out_8
);

  wire button_1_out, button_2_out, button_3_out, button_4_out, comparator_1_eq, comparator_2_eq,
       comparator_3_eq, comparator_4_eq, not_1_out, not_2_out, part_a_1_out_5, part_a_1_out_7;
  wire [2:0] counter_1_q, counter_2_q;

  Part_A part_a_1 (.S1(S2), .S2(S1), .S3(S4), .S4(S3), .out_5(part_a_1_out_5), .out_7(part_a_1_out_7));  // open: out_6
  Button button_1 (.out(button_1_out));
  Button button_2 (.out(button_2_out));
  Counter #(.width(3), .max('h7)) counter_1 (
    .count(part_a_1_out_5), .Q(counter_1_q), .clk(button_3_out), .clr(button_4_out));  // open: load, D, carry
  Button button_3 (.out(button_3_out));
  Button button_4 (.out(button_4_out));
  Counter #(.width(3), .max('h7)) counter_2 (
    .count(part_a_1_out_7), .Q(counter_2_q), .clk(button_1_out), .clr(button_2_out));  // open: load, D, carry
  Comparator #(.width(3), .mode("unsigned")) comparator_1 (
    .a(counter_2_q), .b(number_of_games), .eq(comparator_1_eq));  // open: gt, lt
  Comparator #(.width(3), .mode("unsigned")) comparator_2 (
    .a(number_of_games), .b(counter_1_q), .eq(comparator_2_eq));  // open: gt, lt
  Comparator #(.width(3)) comparator_3 (.a(number_of_games), .b(in_5), .eq(comparator_3_eq));  // open: gt, lt
  Comparator #(.width(3)) comparator_4 (.a(number_of_games), .b(in_5), .eq(comparator_4_eq));  // open: gt, lt
  not not_1 (not_1_out, comparator_3_eq);
  not not_2 (not_2_out, comparator_4_eq);
  and and_1 (out_7, comparator_1_eq, not_1_out);
  and and_2 (out_8, not_2_out, comparator_2_eq);

  // Notes on the sheet:
  //   Part B
  //   Play P
  //   Player Q
  //   Update the count (clock)
  //   Update the count (clock)
  //   Reset the count to 0
  //   Reset the count to 0
endmodule

module Decorder (
  input  S2_S4,
  input  S1_S3,
  output Rock,
  output Scissors,
  output Paper,
  output out_6
);

  wire not_1_out, not_2_out;

  not not_1 (not_1_out, S2_S4);
  not not_2 (not_2_out, S1_S3);
  and and_1 (Rock, not_1_out, not_2_out);
  and and_2 (Scissors, not_2_out, S2_S4);
  and and_3 (Paper, S1_S3, not_1_out);
  and and_4 (out_6, S1_S3, S2_S4);
endmodule

module Selector (
  input  in_1,
  input  in_2,
  input  in_3,
  input  in_4,
  input  in_5,
  input  in_6,
  output out_7
);

  wire and_1_out, and_2_out, and_3_out;

  and and_1 (and_1_out, in_1, in_2);
  and and_2 (and_2_out, in_3, in_4);
  and and_3 (and_3_out, in_5, in_6);
  or or_1 (out_7, and_1_out, and_2_out, and_3_out);

  // Notes on the sheet:
  //   r
  //   s
  //   p
endmodule

module Part_A (
  input  S1,
  input  S2,
  input  S3,
  input  S4,
  output out_5,
  output out_6,
  output out_7
);

  wire decorder_1_paper, decorder_1_rock, decorder_1_scissors, decorder_2_paper, decorder_2_rock,
       decorder_2_scissors;

  Decorder decorder_1 (
    .S2_S4(S2), .S1_S3(S1), .Rock(decorder_1_rock), .Scissors(decorder_1_scissors), .Paper(decorder_1_paper));  // open: out_6
  Decorder decorder_2 (
    .S2_S4(S4), .S1_S3(S3), .Rock(decorder_2_rock), .Scissors(decorder_2_scissors), .Paper(decorder_2_paper));  // open: out_6
  LED led_1 (.in(out_5));
  Selector selector_1 (
    .in_1(decorder_1_rock), .in_2(decorder_2_scissors), .in_3(decorder_1_scissors), .in_4(decorder_2_paper),
    .in_5(decorder_1_paper), .in_6(decorder_2_rock), .out_7(out_5));
  LED led_2 (.in(out_6));
  Ties____Selector ties_selector_1 (
    .in_1(decorder_1_rock), .in_2(decorder_2_rock), .in_3(decorder_1_scissors), .in_4(decorder_2_scissors),
    .in_5(decorder_1_paper), .in_6(decorder_2_paper), .out_7(out_6));
  Selector selector_2 (
    .in_1(decorder_2_rock), .in_2(decorder_1_scissors), .in_3(decorder_2_scissors), .in_4(decorder_1_paper),
    .in_5(decorder_2_paper), .in_6(decorder_1_rock), .out_7(out_7));
  LED led_3 (.in(out_7));

  // Notes on the sheet:
  //   Part A
  //   Player P
  //   Player Q
  //   LED light up means Player P win
  //   LED light up means Tie, no win, no lose
  //   LED light up means Player Q win
endmodule

module Ties____Selector (
  input  in_1,
  input  in_2,
  input  in_3,
  input  in_4,
  input  in_5,
  input  in_6,
  output out_7
);

  wire and_1_out, and_2_out, and_3_out;

  and and_1 (and_1_out, in_1, in_2);
  and and_2 (and_2_out, in_3, in_4);
  and and_3 (and_3_out, in_5, in_6);
  or or_1 (out_7, and_1_out, and_2_out, and_3_out);

  // Notes on the sheet:
  //   r
  //   s
  //   p
endmodule
